// Logisim project 8bit_cpu.circ as structural Verilog: 52 circuits, main circuit main
module main (
  input  [7:0] START_FROM,
  input  RESET,
  input  SHOW_MEM
);

  wire alu_8bit_1_zero, clock_1_out, control_unit_1_c0, control_unit_1_hlt, control_unit_1_ir_write,
       control_unit_1_pc_write, control_unit_1_reg_a_src, control_unit_1_reg_a_write,
       control_unit_1_reg_b_write, control_unit_1_we;
  wire [1:0] control_unit_1_pc_src, control_unit_1_ram_src;
  wire [2:0] control_unit_1_alu_op;
  wire [3:0] instruction_register_1_opcode, instruction_register_1_operand;
  wire [7:0] alu_8bit_1_f, bit_extender_1_out, bit_extender_2_out, mp_2to1_8bit_1_d, mp_4to1_8bit_1_d,
       program_counter_1_pc_out, ram_1_dout, register_file_1_a_out, register_file_1_b_out;

  LED led_1 (.in(control_unit_1_hlt));
  Clock clock_1 (.out(clock_1_out));
  Control_Unit control_unit_1 (
    .OPCODE(instruction_register_1_opcode), .RESET(RESET), .CLK(clock_1_out), .ZERO(alu_8bit_1_zero),
    .PC_Src(control_unit_1_pc_src[0]), .IR_Write(control_unit_1_ir_write), .C0(control_unit_1_c0),
    .ALU_OP(control_unit_1_alu_op), .HLT(control_unit_1_hlt), .RAM_Src1(control_unit_1_ram_src[1]),
    .REG_A_Write(control_unit_1_reg_a_write), .REG_A_Src(control_unit_1_reg_a_src),
    .REG_B_Write(control_unit_1_reg_b_write), .WE(control_unit_1_we), .RAM_Src(control_unit_1_ram_src[0]),
    .PC_Write(control_unit_1_pc_write), .PC_Src1(control_unit_1_pc_src[1]));
  // Probe on instruction_register_1_opcode
  assign bit_extender_1_out = {{4{1'b0}}, instruction_register_1_operand};  // Bit_Extender bit_extender_1
  // Probe on START_FROM
  Program_Counter program_counter_1 (
    .PC_Reset(RESET), .CLK(clock_1_out), .PC_Write(control_unit_1_pc_write), .ADR2(register_file_1_b_out),
    .ADR1(bit_extender_1_out), .START_FROM(START_FROM), .PC_Src(control_unit_1_pc_src),
    .PC_Out(program_counter_1_pc_out));
  Instruction_Register instruction_register_1 (
    .CLK(clock_1_out), .IR_Reset(RESET), .IN_RAM(ram_1_dout), .IR_Write(control_unit_1_ir_write),
    .OPCODE(instruction_register_1_opcode), .OPERAND(instruction_register_1_operand));
  // Probe on program_counter_1_pc_out
  // Probe on instruction_register_1_operand
  assign bit_extender_2_out = {{4{1'b0}}, instruction_register_1_operand};  // Bit_Extender bit_extender_2
  MP_4to1_8bit mp_4to1_8bit_1 (
    .I3({8{1'b0}}), .I2(register_file_1_b_out), .I1(bit_extender_2_out), .I0(program_counter_1_pc_out),
    .E(1'b1), .S(control_unit_1_ram_src), .D(mp_4to1_8bit_1_d));
  MP_2to1_8bit mp_2to1_8bit_1 (.I1(8'hf), .I0(mp_4to1_8bit_1_d), .E(1'b1), .S(SHOW_MEM), .D(mp_2to1_8bit_1_d));
  RAM ram_1 (
    .addr(mp_2to1_8bit_1_d), .we(control_unit_1_we), .oe(1'b1), .clk(clock_1_out),
    .din(register_file_1_a_out), .dout(ram_1_dout));
  // Probe on register_file_1_a_out
  // BCD_to_7_Segment_decoder bcd_to_7_segment_decoder_1: pin names not known
  _7_Segment_Display u_7_segment_display_1 ();  // open: g, f, a, b, e, d, c, dp
  // Binary_to_BCD_converter #(.binvalue(8)) binary_to_bcd_converter_1: pin names not known
  Register_File register_file_1 (
    .DATA_IN(ram_1_dout), .ALU_IN(alu_8bit_1_f), .REG_A_Src(control_unit_1_reg_a_src), .CLK(clock_1_out),
    .RESET(RESET), .REG_A_Write(control_unit_1_reg_a_write), .REG_B_Write(control_unit_1_reg_b_write),
    .A_OUT(register_file_1_a_out), .B_OUT(register_file_1_b_out));
  ALU_8bit alu_8bit_1 (
    .A(register_file_1_a_out), .B(register_file_1_b_out), .S(control_unit_1_alu_op), .C0(control_unit_1_c0),
    .F(alu_8bit_1_f), .ZERO(alu_8bit_1_zero));  // open: Cn, F0, F7
  // BCD_to_7_Segment_decoder bcd_to_7_segment_decoder_2: pin names not known
  _7_Segment_Display u_7_segment_display_2 ();  // open: g, f, a, b, e, d, c, dp
  // Probe on register_file_1_b_out
  // BCD_to_7_Segment_decoder bcd_to_7_segment_decoder_3: pin names not known
  _7_Segment_Display u_7_segment_display_3 ();  // open: g, f, a, b, e, d, c, dp
  // Probe on alu_8bit_1_f
endmodule

module DC_1to2 (
  input  E,
  input  S,
  output [1:0] D
);

  wire not_1_out;

  not not_1 (not_1_out, S);
  and and_1 (D[1], E, S);
  and and_2 (D[0], E, not_1_out);
endmodule

module DC_2to4 (
  input  E,
  input  [1:0] S,
  output [3:0] D
);

  wire [1:0] dc_1to2_1_d;

  DC_1to2 dc_1to2_1 (.E(E), .S(S[1]), .D(dc_1to2_1_d));
  DC_1to2 dc_1to2_2 (.E(dc_1to2_1_d[1]), .S(S[0]), .D(D[3:2]));
  DC_1to2 dc_1to2_3 (.E(dc_1to2_1_d[0]), .S(S[0]), .D(D[1:0]));
endmodule

module DC_3to8 (
  input  E,
  input  [2:0] S,
  output [7:0] D
);

  wire [1:0] dc_1to2_1_d;

  DC_1to2 dc_1to2_1 (.E(E), .S(S[2]), .D(dc_1to2_1_d));
  DC_2to4 dc_2to4_1 (.S(S[1:0]), .E(dc_1to2_1_d[1]), .D(D[7:4]));
  DC_2to4 dc_2to4_2 (.S(S[1:0]), .E(dc_1to2_1_d[0]), .D(D[3:0]));
endmodule

module DC_4to16 (
  input  E,
  input  [3:0] S,
  output [15:0] D
);

  wire [1:0] dc_1to2_1_d;

  DC_1to2 dc_1to2_1 (.E(E), .S(S[3]), .D(dc_1to2_1_d));
  DC_3to8 dc_3to8_1 (.S(S[2:0]), .E(dc_1to2_1_d[1]), .D(D[15:8]));
  DC_3to8 dc_3to8_2 (.S(S[2:0]), .E(dc_1to2_1_d[0]), .D(D[7:0]));
endmodule

module MP_2to1 (
  input  E,
  input  [1:0] I,
  input  S,
  output D
);

  wire and_1_out, and_2_out, not_1_out;

  not not_1 (not_1_out, S);
  and and_1 (and_1_out, E, I[1], S);
  and and_2 (and_2_out, E, I[0], not_1_out);
  or or_1 (D, and_1_out, and_2_out);
endmodule

module MP_4to1 (
  input  E,
  input  [3:0] I,
  input  [1:0] S,
  output D
);

  wire [1:0] mp_2to1_2_d;

  MP_2to1 mp_2to1_1 (.S(S[0]), .E(E), .I(I[3:2]), .D(mp_2to1_2_d[1]));
  MP_2to1 mp_2to1_2 (.S(S[0]), .E(E), .I(I[1:0]), .D(mp_2to1_2_d[0]));
  MP_2to1 mp_2to1_3 (.S(S[1]), .E(E), .I(mp_2to1_2_d), .D(D));
endmodule

module MP_2to1_8bit (
  input  E,
  input  [7:0] I1,
  input  [7:0] I0,
  input  S,
  output [7:0] D
);

  MP_2to1 mp_2to1_1 (.S(S), .E(E), .I({I1[7], I0[7]}), .D(D[7]));
  MP_2to1 mp_2to1_2 (.S(S), .E(E), .I({I1[6], I0[6]}), .D(D[6]));
  MP_2to1 mp_2to1_3 (.S(S), .E(E), .I({I1[5], I0[5]}), .D(D[5]));
  MP_2to1 mp_2to1_4 (.S(S), .E(E), .I({I1[4], I0[4]}), .D(D[4]));
  MP_2to1 mp_2to1_5 (.S(S), .E(E), .I({I1[3], I0[3]}), .D(D[3]));
  MP_2to1 mp_2to1_6 (.S(S), .E(E), .I({I1[2], I0[2]}), .D(D[2]));
  MP_2to1 mp_2to1_7 (.S(S), .E(E), .I({I1[1], I0[1]}), .D(D[1]));
  MP_2to1 mp_2to1_8 (.S(S), .E(E), .I({I1[0], I0[0]}), .D(D[0]));
endmodule

module MP_4to1_8bit (
  input  E,
  input  [7:0] I3,
  input  [7:0] I2,
  input  [7:0] I1,
  input  [7:0] I0,
  input  [1:0] S,
  output [7:0] D
);

  MP_4to1 mp_4to1_1 (.E(E), .S(S), .I({I3[7], I2[7], I1[7], I0[7]}), .D(D[7]));
  MP_4to1 mp_4to1_2 (.E(E), .S(S), .I({I3[6], I2[6], I1[6], I0[6]}), .D(D[6]));
  MP_4to1 mp_4to1_3 (.E(E), .S(S), .I({I3[5], I2[5], I1[5], I0[5]}), .D(D[5]));
  MP_4to1 mp_4to1_4 (.E(E), .S(S), .I({I3[4], I2[4], I1[4], I0[4]}), .D(D[4]));
  MP_4to1 mp_4to1_5 (.E(E), .S(S), .I({I3[3], I2[3], I1[3], I0[3]}), .D(D[3]));
  MP_4to1 mp_4to1_6 (.E(E), .S(S), .I({I3[2], I2[2], I1[2], I0[2]}), .D(D[2]));
  MP_4to1 mp_4to1_7 (.E(E), .S(S), .I({I3[1], I2[1], I1[1], I0[1]}), .D(D[1]));
  MP_4to1 mp_4to1_8 (.E(E), .S(S), .I({I3[0], I2[0], I1[0], I0[0]}), .D(D[0]));
endmodule

module HEX_to_7SEG (
  input  ENABLE,
  input  [3:0] NUM,
  output A,
  output B,
  output C,
  output D,
  output E,
  output F,
  output G
);

  wire [15:0] dc_4to16_1_d;

  DC_4to16 dc_4to16_1 (.S(NUM), .E(ENABLE), .D(dc_4to16_1_d));
  or or_1 (A, dc_4to16_1_d[0], dc_4to16_1_d[2], dc_4to16_1_d[3], dc_4to16_1_d[5], dc_4to16_1_d[6], dc_4to16_1_d[7], dc_4to16_1_d[8], dc_4to16_1_d[9], dc_4to16_1_d[10], dc_4to16_1_d[12], dc_4to16_1_d[14], dc_4to16_1_d[15]);
  _7_Segment_Display u_7_segment_display_1 (.g(G), .f(F), .a(A), .b(B), .e(E), .d(D), .c(C));  // open: dp
  or or_2 (B, dc_4to16_1_d[0], dc_4to16_1_d[1], dc_4to16_1_d[2], dc_4to16_1_d[3], dc_4to16_1_d[4], dc_4to16_1_d[7], dc_4to16_1_d[8], dc_4to16_1_d[9], dc_4to16_1_d[10], dc_4to16_1_d[13]);
  or or_3 (C, dc_4to16_1_d[0], dc_4to16_1_d[1], dc_4to16_1_d[3], dc_4to16_1_d[4], dc_4to16_1_d[5], dc_4to16_1_d[6], dc_4to16_1_d[7], dc_4to16_1_d[8], dc_4to16_1_d[9], dc_4to16_1_d[10], dc_4to16_1_d[11], dc_4to16_1_d[13]);
  or or_4 (D, dc_4to16_1_d[0], dc_4to16_1_d[2], dc_4to16_1_d[3], dc_4to16_1_d[5], dc_4to16_1_d[6], dc_4to16_1_d[8], dc_4to16_1_d[9], dc_4to16_1_d[11], dc_4to16_1_d[12], dc_4to16_1_d[13], dc_4to16_1_d[14]);
  or or_5 (E, dc_4to16_1_d[0], dc_4to16_1_d[2], dc_4to16_1_d[6], dc_4to16_1_d[8], dc_4to16_1_d[10], dc_4to16_1_d[11], dc_4to16_1_d[12], dc_4to16_1_d[13], dc_4to16_1_d[14], dc_4to16_1_d[15]);
  or or_6 (F, dc_4to16_1_d[0], dc_4to16_1_d[4], dc_4to16_1_d[5], dc_4to16_1_d[6], dc_4to16_1_d[8], dc_4to16_1_d[9], dc_4to16_1_d[10], dc_4to16_1_d[11], dc_4to16_1_d[12], dc_4to16_1_d[14], dc_4to16_1_d[15]);
  or or_7 (G, dc_4to16_1_d[2], dc_4to16_1_d[3], dc_4to16_1_d[4], dc_4to16_1_d[5], dc_4to16_1_d[6], dc_4to16_1_d[8], dc_4to16_1_d[9], dc_4to16_1_d[10], dc_4to16_1_d[11], dc_4to16_1_d[13], dc_4to16_1_d[14], dc_4to16_1_d[15]);
endmodule

module INC_1bit (
  input  Ai,
  input  Ci,
  output Fi,
  output Ci_next
);

  xor xor_1 (Fi, Ai, Ci);
  and and_1 (Ci_next, Ai, Ci);
endmodule

module INC_4bit (
  input  [3:0] A,
  input  Cin,
  output Cout,
  output [3:0] F
);

  wire inc_1bit_2_ci_next, inc_1bit_3_ci_next, inc_1bit_4_ci_next;

  INC_1bit inc_1bit_1 (.Ci(inc_1bit_2_ci_next), .Ai(A[3]), .Fi(F[3]), .Ci_next(Cout));
  INC_1bit inc_1bit_2 (.Ci(inc_1bit_3_ci_next), .Ai(A[2]), .Fi(F[2]), .Ci_next(inc_1bit_2_ci_next));
  INC_1bit inc_1bit_3 (.Ci(inc_1bit_4_ci_next), .Ai(A[1]), .Fi(F[1]), .Ci_next(inc_1bit_3_ci_next));
  INC_1bit inc_1bit_4 (.Ci(Cin), .Ai(A[0]), .Fi(F[0]), .Ci_next(inc_1bit_4_ci_next));
endmodule

module INC_8bit (
  input  [7:0] A,
  input  Cin,
  output Cout,
  output [7:0] F
);

  wire inc_4bit_2_cout;

  INC_4bit inc_4bit_1 (.A(A[7:4]), .Cin(inc_4bit_2_cout), .Cout(Cout), .F(F[7:4]));
  INC_4bit inc_4bit_2 (.A(A[3:0]), .Cin(Cin), .Cout(inc_4bit_2_cout), .F(F[3:0]));
endmodule

module DEC_1bit (
  input  Ai,
  input  Ein,
  output Eout,
  output Fi
);

  wire inc_1bit_1_fi, not_1_out;

  not not_1 (not_1_out, Ai);
  INC_1bit inc_1bit_1 (.Ci(Ein), .Ai(not_1_out), .Fi(inc_1bit_1_fi), .Ci_next(Eout));
  not not_2 (Fi, inc_1bit_1_fi);
endmodule

module DEC_4bit (
  input  [3:0] A,
  input  Ein,
  output Eout,
  output [3:0] F
);

  wire dec_1bit_2_eout, dec_1bit_3_eout, dec_1bit_4_eout;

  DEC_1bit dec_1bit_1 (.Ai(A[3]), .Ein(dec_1bit_2_eout), .Eout(Eout), .Fi(F[3]));
  DEC_1bit dec_1bit_2 (.Ai(A[2]), .Ein(dec_1bit_3_eout), .Eout(dec_1bit_2_eout), .Fi(F[2]));
  DEC_1bit dec_1bit_3 (.Ai(A[1]), .Ein(dec_1bit_4_eout), .Eout(dec_1bit_3_eout), .Fi(F[1]));
  DEC_1bit dec_1bit_4 (.Ai(A[0]), .Ein(Ein), .Eout(dec_1bit_4_eout), .Fi(F[0]));
endmodule

module DEC_8bit (
  input  [7:0] A,
  input  Ein,
  output Eout,
  output [7:0] F
);

  wire dec_4bit_2_eout;

  DEC_4bit dec_4bit_1 (.A(A[7:4]), .Ein(dec_4bit_2_eout), .F(F[7:4]), .Eout(Eout));
  DEC_4bit dec_4bit_2 (.A(A[3:0]), .Ein(Ein), .F(F[3:0]), .Eout(dec_4bit_2_eout));
endmodule

module ADD_1bit (
  input  Ai,
  input  Bi,
  input  Cin,
  output Cout,
  output Fi
);

  wire and_1_out, and_2_out, xor_1_out;

  xor xor_1 (xor_1_out, Ai, Bi);
  xor xor_2 (Fi, xor_1_out, Cin);
  and and_1 (and_1_out, Bi, Ai);
  and and_2 (and_2_out, Cin, xor_1_out);
  or or_1 (Cout, and_1_out, and_2_out);
endmodule

module ADD_4bit (
  input  [3:0] A,
  input  [3:0] B,
  input  Cin,
  output Cout,
  output [3:0] F
);

  wire add_1bit_2_cout, add_1bit_3_cout, add_1bit_4_cout;

  ADD_1bit add_1bit_1 (.Ai(A[3]), .Bi(B[3]), .Cin(add_1bit_2_cout), .Fi(F[3]), .Cout(Cout));
  ADD_1bit add_1bit_2 (.Ai(A[2]), .Bi(B[2]), .Cin(add_1bit_3_cout), .Fi(F[2]), .Cout(add_1bit_2_cout));
  ADD_1bit add_1bit_3 (.Ai(A[1]), .Bi(B[1]), .Cin(add_1bit_4_cout), .Fi(F[1]), .Cout(add_1bit_3_cout));
  ADD_1bit add_1bit_4 (.Ai(A[0]), .Bi(B[0]), .Cin(Cin), .Fi(F[0]), .Cout(add_1bit_4_cout));
endmodule

module ADD_8bit (
  input  [7:0] A,
  input  [7:0] B,
  input  Cin,
  output Cout,
  output [7:0] F
);

  wire add_4bit_2_cout;

  ADD_4bit add_4bit_1 (.A(A[7:4]), .B(B[7:4]), .Cin(add_4bit_2_cout), .Cout(Cout), .F(F[7:4]));
  ADD_4bit add_4bit_2 (.A(A[3:0]), .B(B[3:0]), .Cin(Cin), .Cout(add_4bit_2_cout), .F(F[3:0]));
endmodule

module SUB_1bit (
  input  Ai,
  input  Bi,
  input  Ein,
  output Eout,
  output Fi
);

  wire and_1_out, and_2_out, not_1_out, not_2_out, xor_1_out;

  xor xor_1 (xor_1_out, Ai, Bi);
  xor xor_2 (Fi, xor_1_out, Ein);
  not not_1 (not_1_out, Ai);
  not not_2 (not_2_out, xor_1_out);
  and and_1 (and_1_out, Bi, not_1_out);
  and and_2 (and_2_out, Ein, not_2_out);
  or or_1 (Eout, and_1_out, and_2_out);
endmodule

module SUB_4bit (
  input  [3:0] A,
  input  [3:0] B,
  input  Ein,
  output Eout,
  output [3:0] F
);

  wire sub_1bit_2_eout, sub_1bit_3_eout, sub_1bit_4_eout;

  SUB_1bit sub_1bit_1 (.Ai(A[3]), .Bi(B[3]), .Ein(sub_1bit_2_eout), .Fi(F[3]), .Eout(Eout));
  SUB_1bit sub_1bit_2 (.Ai(A[2]), .Bi(B[2]), .Ein(sub_1bit_3_eout), .Fi(F[2]), .Eout(sub_1bit_2_eout));
  SUB_1bit sub_1bit_3 (.Ai(A[1]), .Bi(B[1]), .Ein(sub_1bit_4_eout), .Fi(F[1]), .Eout(sub_1bit_3_eout));
  SUB_1bit sub_1bit_4 (.Ai(A[0]), .Bi(B[0]), .Ein(Ein), .Fi(F[0]), .Eout(sub_1bit_4_eout));
endmodule

module SUB_8bit (
  input  [7:0] A,
  input  [7:0] B,
  input  Ein,
  output Eout,
  output [7:0] F
);

  wire sub_4bit_2_eout;

  SUB_4bit sub_4bit_1 (.A(A[7:4]), .B(B[7:4]), .Ein(sub_4bit_2_eout), .Eout(Eout), .F(F[7:4]));
  SUB_4bit sub_4bit_2 (.A(A[3:0]), .B(B[3:0]), .Ein(Ein), .Eout(sub_4bit_2_eout), .F(F[3:0]));
endmodule

module LOG_1bit (
  input  Ai,
  input  Bi,
  input  [1:0] S,
  output Fi
);

  wire and_1_out, and_2_out, and_3_out, and_4_out, and_5_out, not_1_out, or_1_out, xor_1_out;
  wire [3:0] dc_2to4_1_d;

  and and_1 (and_1_out, Ai, Bi);
  or or_1 (or_1_out, Ai, Bi);
  not not_1 (not_1_out, Ai);
  DC_2to4 dc_2to4_1 (.S(S), .E(1'b1), .D(dc_2to4_1_d));
  xor xor_1 (xor_1_out, Ai, Bi);
  and and_2 (and_2_out, and_1_out, dc_2to4_1_d[0]);
  and and_3 (and_3_out, or_1_out, dc_2to4_1_d[1]);
  and and_4 (and_4_out, xor_1_out, dc_2to4_1_d[2]);
  and and_5 (and_5_out, not_1_out, dc_2to4_1_d[3]);
  or or_2 (Fi, and_2_out, and_3_out, and_4_out, and_5_out);
endmodule

module LOG_4bit (
  input  [3:0] A,
  input  [3:0] B,
  input  [1:0] S,
  output [3:0] F
);

  LOG_1bit log_1bit_1 (.S(S), .Ai(A[3]), .Bi(B[3]), .Fi(F[3]));
  LOG_1bit log_1bit_2 (.S(S), .Ai(A[2]), .Bi(B[2]), .Fi(F[2]));
  LOG_1bit log_1bit_3 (.S(S), .Ai(A[1]), .Bi(B[1]), .Fi(F[1]));
  LOG_1bit log_1bit_4 (.S(S), .Ai(A[0]), .Bi(B[0]), .Fi(F[0]));
endmodule

module LOG_8bit (
  input  [7:0] A,
  input  [7:0] B,
  input  [1:0] S,
  output [7:0] F
);

  LOG_4bit log_4bit_1 (.A(A[7:4]), .B(B[7:4]), .S(S), .F(F[7:4]));
  LOG_4bit log_4bit_2 (.A(A[3:0]), .B(B[3:0]), .S(S), .F(F[3:0]));
endmodule

module ARI_8bit (
  input  [7:0] A,
  input  [7:0] B,
  input  C0,
  input  [1:0] S,
  output C,
  output [7:0] F
);

  wire [3:0] inc_8bit_1_cout;
  wire [7:0] add_8bit_1_f, dec_8bit_1_f, inc_8bit_1_f, sub_8bit_1_f;

  INC_8bit inc_8bit_1 (.A(A), .Cin(C0), .Cout(inc_8bit_1_cout[0]), .F(inc_8bit_1_f));
  ADD_8bit add_8bit_1 (.A(A), .B(B), .Cin(C0), .Cout(inc_8bit_1_cout[1]), .F(add_8bit_1_f));
  MP_4to1_8bit mp_4to1_8bit_1 (
    .I3(sub_8bit_1_f), .I2(dec_8bit_1_f), .I1(add_8bit_1_f), .I0(inc_8bit_1_f), .E(1'b1), .S(S), .D(F));
  DEC_8bit dec_8bit_1 (.A(A), .Ein(C0), .Eout(inc_8bit_1_cout[2]), .F(dec_8bit_1_f));
  SUB_8bit sub_8bit_1 (.A(A), .B(B), .Ein(C0), .Eout(inc_8bit_1_cout[3]), .F(sub_8bit_1_f));
  MP_4to1 mp_4to1_1 (.E(1'b1), .S(S), .I(inc_8bit_1_cout), .D(C));
endmodule

module ALU_8bit (
  input  C0,
  input  [7:0] A,
  input  [7:0] B,
  input  [2:0] S,
  output Cn,
  output F0,
  output F7,
  output [7:0] F,
  output ZERO
);

  wire [7:0] ari_8bit_1_f, log_8bit_1_f;

  ARI_8bit ari_8bit_1 (.S(S[1:0]), .A(A), .B(B), .C0(C0), .F(ari_8bit_1_f), .C(Cn));
  LOG_8bit log_8bit_1 (.A(A), .B(B), .S(S[1:0]), .F(log_8bit_1_f));
  MP_4to1_8bit mp_4to1_8bit_1 (
    .I3({8{1'b0}}), .I2({8{1'b0}}), .I1(log_8bit_1_f), .I0(ari_8bit_1_f), .E(1'b1), .S({1'b0, S[2]}), .D(F));
  RAM ram_1 ();  // open: addr, we, oe, clk, din, dout
  Zero_Flag zero_flag_1 (.in_1(F), .out_2(ZERO));

  assign F0 = F[0];
  assign F7 = F[7];
endmodule

module RS_FF_noCLK (
  input  R,
  input  S,
  output Q,
  output NQ
);

  nor nor_1 (Q, R, NQ);
  nor nor_2 (NQ, Q, S);
endmodule

module D_FF (
  input  Rd,
  input  D,
  input  CLK,
  input  Sd,
  output Q,
  output NQ
);

  wire and_1_out, and_2_out, nor_1_out, nor_2_out, not_1_out, or_1_out, or_2_out, rs_ff_noclk_1_nq,
       rs_ff_noclk_1_q;

  not not_1 (not_1_out, D);
  and and_1 (and_1_out, not_1_out, CLK);
  or or_1 (or_1_out, Rd, and_1_out);
  or or_2 (or_2_out, and_2_out, Sd);
  and and_2 (and_2_out, CLK, D);
  RS_FF_noCLK rs_ff_noclk_1 (.R(or_1_out), .S(or_2_out), .Q(rs_ff_noclk_1_q), .NQ(rs_ff_noclk_1_nq));
  nor nor_1 (nor_1_out, rs_ff_noclk_1_q, CLK);
  nor nor_2 (nor_2_out, CLK, rs_ff_noclk_1_nq);
  RS_FF_noCLK rs_ff_noclk_2 (.R(nor_1_out), .S(nor_2_out), .Q(Q), .NQ(NQ));
endmodule

module D_Latch (
  input  D,
  input  E,
  output Q,
  output NQ
);

  wire and_1_out, and_2_out, not_1_out;

  not not_1 (not_1_out, D);
  and and_1 (and_1_out, not_1_out, E);
  and and_2 (and_2_out, E, D);
  RS_FF_noCLK rs_ff_noclk_1 (.R(and_1_out), .S(and_2_out), .Q(Q), .NQ(NQ));
endmodule

module REG_1bit (
  input  LD,
  input  Ii,
  input  INC,
  input  Cin,
  input  CL,
  input  CLK,
  output Ai,
  output NAi,
  output Cout
);

  wire and_1_out, and_2_out, and_3_out, not_1_out, not_2_out, not_3_out, or_1_out, xor_1_out;

  not not_1 (not_1_out, LD);
  not not_2 (not_2_out, CL);
  and and_1 (and_1_out, LD, Ii);
  xor xor_1 (xor_1_out, Ai, Cin);
  not not_3 (not_3_out, INC);
  and and_2 (and_2_out, INC, xor_1_out);
  or or_1 (or_1_out, and_1_out, and_2_out, and_3_out);
  and and_3 (and_3_out, not_1_out, not_3_out, not_2_out, Ai);
  D_FF d_ff_1 (.D(or_1_out), .CLK(CLK), .Q(Ai), .NQ(NAi));  // open: Rd, Sd
  and and_4 (Cout, Ai, Cin);
endmodule

module REG_8bit (
  input  [7:0] I,
  input  IR,
  input  IL,
  input  LD,
  input  SR,
  input  SL,
  input  CL,
  input  CLK,
  input  INC,
  input  DEC,
  output [7:0] A
);

  wire mp_2to1_1_d, mp_2to1_2_d, mp_2to1_3_d, mp_2to1_4_d, mp_2to1_5_d, mp_2to1_6_d, mp_2to1_7_d,
       mp_4to1_1_d, mp_4to1_2_d, mp_4to1_3_d, mp_4to1_4_d, mp_4to1_5_d, mp_4to1_6_d, mp_4to1_7_d,
       mp_4to1_8_d, or_1_out, or_2_out, reg_1bit_2_nai, reg_1bit_3_nai, reg_1bit_4_nai, reg_1bit_5_nai,
       reg_1bit_6_nai, reg_1bit_7_nai, reg_1bit_8_nai;
  wire [1:0] reg_1bit_2_cout, reg_1bit_3_cout, reg_1bit_4_cout, reg_1bit_5_cout, reg_1bit_6_cout,
       reg_1bit_7_cout, reg_1bit_8_cout;

  or or_1 (or_1_out, SL, SR, LD);
  or or_2 (or_2_out, INC, DEC);
  MP_4to1 mp_4to1_1 (.E(1'b1), .S({SL, SR}), .I({1'b0, A[6], IR, I[7]}), .D(mp_4to1_1_d));
  REG_1bit reg_1bit_1 (
    .Ii(mp_4to1_1_d), .INC(or_2_out), .Cin(mp_2to1_1_d), .CL(CL), .CLK(CLK), .LD(or_1_out), .Ai(A[7]));  // open: NAi, Cout
  MP_2to1 mp_2to1_1 (.S(DEC), .E(1'b1), .I(reg_1bit_2_cout), .D(mp_2to1_1_d));
  MP_4to1 mp_4to1_2 (.E(1'b1), .S({SL, SR}), .I({1'b0, A[5], A[7], I[6]}), .D(mp_4to1_2_d));
  REG_1bit reg_1bit_2 (
    .Ii(mp_4to1_2_d), .INC(or_2_out), .Cin(mp_2to1_2_d), .CL(CL), .CLK(CLK), .LD(or_1_out),
    .NAi(reg_1bit_2_nai), .Ai(A[6]), .Cout(reg_1bit_2_cout[0]));
  and and_1 (reg_1bit_2_cout[1], reg_1bit_2_nai, mp_2to1_2_d);
  MP_2to1 mp_2to1_2 (.S(DEC), .E(1'b1), .I(reg_1bit_3_cout), .D(mp_2to1_2_d));
  and and_2 (reg_1bit_3_cout[1], reg_1bit_3_nai, mp_2to1_3_d);
  MP_4to1 mp_4to1_3 (.E(1'b1), .S({SL, SR}), .I({1'b0, A[4], A[6], I[5]}), .D(mp_4to1_3_d));
  REG_1bit reg_1bit_3 (
    .Ii(mp_4to1_3_d), .INC(or_2_out), .Cin(mp_2to1_3_d), .CL(CL), .CLK(CLK), .LD(or_1_out),
    .NAi(reg_1bit_3_nai), .Ai(A[5]), .Cout(reg_1bit_3_cout[0]));
  MP_2to1 mp_2to1_3 (.S(DEC), .E(1'b1), .I(reg_1bit_4_cout), .D(mp_2to1_3_d));
  MP_4to1 mp_4to1_4 (.E(1'b1), .S({SL, SR}), .I({1'b0, A[3], A[5], I[4]}), .D(mp_4to1_4_d));
  REG_1bit reg_1bit_4 (
    .Ii(mp_4to1_4_d), .INC(or_2_out), .Cin(mp_2to1_4_d), .CL(CL), .CLK(CLK), .LD(or_1_out),
    .NAi(reg_1bit_4_nai), .Ai(A[4]), .Cout(reg_1bit_4_cout[0]));
  and and_3 (reg_1bit_4_cout[1], reg_1bit_4_nai, mp_2to1_4_d);
  MP_2to1 mp_2to1_4 (.S(DEC), .E(1'b1), .I(reg_1bit_5_cout), .D(mp_2to1_4_d));
  MP_4to1 mp_4to1_5 (.E(1'b1), .S({SL, SR}), .I({1'b0, A[2], A[4], I[3]}), .D(mp_4to1_5_d));
  REG_1bit reg_1bit_5 (
    .Ii(mp_4to1_5_d), .INC(or_2_out), .Cin(mp_2to1_5_d), .CL(CL), .CLK(CLK), .LD(or_1_out),
    .NAi(reg_1bit_5_nai), .Ai(A[3]), .Cout(reg_1bit_5_cout[0]));
  and and_4 (reg_1bit_5_cout[1], reg_1bit_5_nai, mp_2to1_5_d);
  MP_2to1 mp_2to1_5 (.S(DEC), .E(1'b1), .I(reg_1bit_6_cout), .D(mp_2to1_5_d));
  MP_4to1 mp_4to1_6 (.E(1'b1), .S({SL, SR}), .I({1'b0, A[1], A[3], I[2]}), .D(mp_4to1_6_d));
  REG_1bit reg_1bit_6 (
    .Ii(mp_4to1_6_d), .INC(or_2_out), .Cin(mp_2to1_6_d), .CL(CL), .CLK(CLK), .LD(or_1_out),
    .NAi(reg_1bit_6_nai), .Ai(A[2]), .Cout(reg_1bit_6_cout[0]));
  and and_5 (reg_1bit_6_cout[1], reg_1bit_6_nai, mp_2to1_6_d);
  MP_2to1 mp_2to1_6 (.S(DEC), .E(1'b1), .I(reg_1bit_7_cout), .D(mp_2to1_6_d));
  and and_6 (reg_1bit_7_cout[1], reg_1bit_7_nai, mp_2to1_7_d);
  MP_4to1 mp_4to1_7 (.E(1'b1), .S({SL, SR}), .I({1'b0, A[0], A[2], I[1]}), .D(mp_4to1_7_d));
  REG_1bit reg_1bit_7 (
    .Ii(mp_4to1_7_d), .INC(or_2_out), .Cin(mp_2to1_7_d), .CL(CL), .CLK(CLK), .LD(or_1_out),
    .NAi(reg_1bit_7_nai), .Ai(A[1]), .Cout(reg_1bit_7_cout[0]));
  MP_2to1 mp_2to1_7 (.S(DEC), .E(1'b1), .I(reg_1bit_8_cout), .D(mp_2to1_7_d));
  MP_4to1 mp_4to1_8 (.E(1'b1), .S({SL, SR}), .I({1'b0, IL, A[1], I[0]}), .D(mp_4to1_8_d));
  REG_1bit reg_1bit_8 (
    .Ii(mp_4to1_8_d), .INC(or_2_out), .Cin(or_2_out), .CL(CL), .CLK(CLK), .LD(or_1_out),
    .NAi(reg_1bit_8_nai), .Ai(A[0]), .Cout(reg_1bit_8_cout[0]));
  and and_7 (reg_1bit_8_cout[1], reg_1bit_8_nai, or_2_out);
endmodule

module Zero_Flag (
  input  [7:0] in_1,
  output out_2
);

  nor nor_1 (out_2, in_1[0], in_1[1], in_1[2], in_1[3], in_1[5], in_1[6], in_1[7], in_1[4]);
endmodule

module All1_Flag (
  input  [7:0] in_1,
  output out_2
);

  and and_1 (out_2, in_1[0], in_1[1], in_1[2], in_1[3], in_1[5], in_1[6], in_1[7], in_1[4]);
endmodule

module Operational_Unit (
  input  [7:0] DATA_IN,
  input  inBUS,
  input  ldR0,
  input  ldR1,
  input  clR2,
  input  ldR2,
  input  clR3,
  input  ldR3,
  input  incR2,
  input  decR3,
  input  rdR0,
  input  rdR1,
  input  rdR2,
  input  rdR3,
  input  clL,
  input  ldL,
  input  CLK,
  input  C0,
  input  [2:0] S,
  input  rdALU,
  input  ldA,
  input  clA,
  input  sr_A,
  input  sl_A,
  input  incA,
  input  irA,
  input  decA,
  input  ilA,
  input  rdA,
  output ALL1,
  output Z,
  output [7:0] DATA_OUT,
  output C,
  output F7,
  output F0
);

  wire [7:0] alu_8bit_1_f, reg_8bit_1_a, reg_8bit_2_a, reg_8bit_3_a, reg_8bit_4_a, reg_8bit_5_a, reg_8bit_6_a;

  REG_8bit reg_8bit_1 (
    .INC(1'b0), .DEC(1'b0), .IL(1'b0), .IR(1'b0), .LD(ldR0), .SR(1'b0), .SL(1'b0), .I(DATA_OUT), .CL(1'b0),
    .CLK(CLK), .A(reg_8bit_1_a));
  assign DATA_OUT = rdR0 ? reg_8bit_1_a : 8'bz;  // Controlled_Buffer controlled_buffer_1
  REG_8bit reg_8bit_2 (
    .INC(1'b0), .DEC(1'b0), .IL(1'b0), .IR(1'b0), .LD(ldL), .SR(1'b0), .SL(1'b0), .I(DATA_OUT), .CL(clL),
    .CLK(CLK), .A(reg_8bit_2_a));
  ALU_8bit alu_8bit_1 (
    .A(reg_8bit_2_a), .B(DATA_OUT), .S(S), .C0(C0), .Cn(C), .F0(F0), .F7(F7), .F(alu_8bit_1_f));  // open: ZERO
  REG_8bit reg_8bit_3 (
    .INC(incA), .DEC(decA), .IL(ilA), .IR(irA), .LD(ldA), .SR(sr_A), .SL(sl_A), .I(alu_8bit_1_f), .CL(clA),
    .CLK(CLK), .A(reg_8bit_3_a));
  assign DATA_OUT = rdA ? reg_8bit_3_a : 8'bz;  // Controlled_Buffer controlled_buffer_2
  assign DATA_OUT = inBUS ? DATA_IN : 8'bz;  // Controlled_Buffer controlled_buffer_3
  REG_8bit reg_8bit_4 (
    .INC(1'b0), .DEC(1'b0), .IL(1'b0), .IR(1'b0), .LD(ldR1), .SR(1'b0), .SL(1'b0), .I(DATA_OUT), .CL(1'b0),
    .CLK(CLK), .A(reg_8bit_4_a));
  assign DATA_OUT = rdR1 ? reg_8bit_4_a : 8'bz;  // Controlled_Buffer controlled_buffer_4
  assign DATA_OUT = rdALU ? alu_8bit_1_f : 8'bz;  // Controlled_Buffer controlled_buffer_5
  REG_8bit reg_8bit_5 (
    .INC(incR2), .DEC(1'b0), .IL(1'b0), .IR(1'b0), .LD(ldR2), .SR(1'b0), .SL(1'b0), .I(DATA_OUT), .CL(clR2),
    .CLK(CLK), .A(reg_8bit_5_a));
  assign DATA_OUT = rdR2 ? reg_8bit_5_a : 8'bz;  // Controlled_Buffer controlled_buffer_6
  All1_Flag all1_flag_1 (.in_1(reg_8bit_5_a), .out_2(ALL1));
  REG_8bit reg_8bit_6 (
    .INC(1'b0), .DEC(decR3), .IL(1'b0), .IR(1'b0), .LD(ldR3), .SR(1'b0), .SL(1'b0), .I(DATA_OUT), .CL(clR3),
    .CLK(CLK), .A(reg_8bit_6_a));
  assign DATA_OUT = rdR3 ? reg_8bit_6_a : 8'bz;  // Controlled_Buffer controlled_buffer_7
  Zero_Flag zero_flag_1 (.in_1(reg_8bit_6_a), .out_2(Z));

  // Notes on the sheet:
  //   R0
  //   L
  //   A
  //   R1
  //   R2
  //   R3
endmodule

module Control_Unit_ADDABS2 (
  input  F7,
  input  ADDABS2,
  input  RESET,
  input  CLK,
  output rdR0,
  output clA,
  output ldL,
  output rdA,
  output rdR1,
  output S0,
  output ldA,
  output ldR3,
  output S2,
  output C0,
  output rdALU,
  output S1
);

  wire and_1_out, and_2_out, and_3_out, and_4_out, and_5_out, and_6_out, d_ff_1_q, d_ff_2_q, d_ff_5_q,
       d_ff_7_q, d_ff_8_q, d_ff_9_q, d_ff_10_q, d_ff_11_q, d_ff_12_q, not_1_out, not_2_out, not_3_out,
       or_1_out, or_2_out, or_3_out;

  or or_1 (or_1_out, and_1_out, ldR3);
  D_FF d_ff_1 (.D(or_1_out), .CLK(CLK), .Sd(RESET), .Q(d_ff_1_q));  // open: Rd, NQ
  D_FF d_ff_2 (.D(d_ff_11_q), .CLK(CLK), .Rd(RESET), .Q(d_ff_2_q));  // open: Sd, NQ
  not not_1 (not_1_out, ADDABS2);
  and and_1 (and_1_out, not_1_out, d_ff_1_q);
  and and_2 (and_2_out, ADDABS2, d_ff_1_q);
  or or_2 (or_2_out, d_ff_8_q, d_ff_12_q);
  D_FF d_ff_3 (.D(or_2_out), .CLK(CLK), .Rd(RESET), .Q(rdR1));  // open: Sd, NQ
  D_FF d_ff_4 (.D(and_2_out), .CLK(CLK), .Rd(RESET), .Q(clA));  // open: Sd, NQ
  D_FF d_ff_5 (.D(rdR1), .CLK(CLK), .Rd(RESET), .Q(d_ff_5_q));  // open: Sd, NQ
  or or_3 (or_3_out, d_ff_9_q, d_ff_2_q);
  D_FF d_ff_6 (.D(or_3_out), .CLK(CLK), .Rd(RESET), .Q(ldR3));  // open: Sd, NQ
  D_FF d_ff_7 (.D(clA), .CLK(CLK), .Rd(RESET), .Q(d_ff_7_q));  // open: Sd, NQ
  not not_2 (not_2_out, F7);
  not not_3 (not_3_out, F7);
  and and_3 (and_3_out, not_3_out, d_ff_5_q);
  and and_4 (and_4_out, F7, d_ff_5_q);
  and and_5 (and_5_out, not_2_out, d_ff_7_q);
  and and_6 (and_6_out, F7, d_ff_7_q);
  D_FF d_ff_8 (.D(and_5_out), .CLK(CLK), .Rd(RESET), .Q(d_ff_8_q));  // open: Sd, NQ
  D_FF d_ff_9 (.D(and_3_out), .CLK(CLK), .Rd(RESET), .Q(d_ff_9_q));  // open: Sd, NQ
  D_FF d_ff_10 (.D(and_6_out), .CLK(CLK), .Rd(RESET), .Q(d_ff_10_q));  // open: Sd, NQ
  D_FF d_ff_11 (.D(and_4_out), .CLK(CLK), .Rd(RESET), .Q(d_ff_11_q));  // open: Sd, NQ
  or or_4 (C0, d_ff_12_q, d_ff_2_q);
  D_FF d_ff_12 (.D(d_ff_10_q), .CLK(CLK), .Rd(RESET), .Q(d_ff_12_q));  // open: Sd, NQ
  or or_5 (rdALU, d_ff_10_q, d_ff_11_q);
  or or_6 (ldL, clA, d_ff_10_q, rdR1, d_ff_11_q, d_ff_2_q);
  or or_7 (rdA, d_ff_8_q, d_ff_12_q, d_ff_9_q, d_ff_2_q, ldR3);
  or or_8 (S0, d_ff_8_q, d_ff_10_q, d_ff_12_q, d_ff_9_q, d_ff_11_q, d_ff_2_q);
  or or_9 (ldA, d_ff_8_q, d_ff_12_q, d_ff_9_q, d_ff_2_q);

  assign rdR0 = clA;
  assign S1 = rdALU;
  assign S2 = rdALU;

  // Notes on the sheet:
  //   K0
  //   K10
  //   K6
  //   K1
  //   K7
  //   K11
  //   K2
  //   K3
  //   K8
  //   K4
  //   K9
  //   K5
endmodule

module ADDABS2 (
  input  [7:0] in_1,
  input  in_2,
  input  ldR0,
  input  ldR1,
  input  rdR0,
  input  rdR3,
  input  rdR1,
  input  ADD_ABS2,
  input  RESET,
  output [7:0] out_10
);

  wire clock_1_out, control_unit_addabs2_1_c0, control_unit_addabs2_1_cla, control_unit_addabs2_1_lda,
       control_unit_addabs2_1_ldl, control_unit_addabs2_1_ldr3, control_unit_addabs2_1_rda,
       control_unit_addabs2_1_rdalu, control_unit_addabs2_1_rdr0, control_unit_addabs2_1_rdr1,
       operational_unit_1_f7, or_1_out, or_2_out;
  wire [2:0] control_unit_addabs2_1_s0;

  Clock clock_1 (.out(clock_1_out));
  Control_Unit_ADDABS2 control_unit_addabs2_1 (
    .RESET(RESET), .CLK(clock_1_out), .ADDABS2(ADD_ABS2), .F7(operational_unit_1_f7),
    .S1(control_unit_addabs2_1_s0[1]), .S2(control_unit_addabs2_1_s0[2]), .ldL(control_unit_addabs2_1_ldl),
    .rdA(control_unit_addabs2_1_rda), .rdALU(control_unit_addabs2_1_rdalu),
    .S0(control_unit_addabs2_1_s0[0]), .ldA(control_unit_addabs2_1_lda), .rdR1(control_unit_addabs2_1_rdr1),
    .rdR0(control_unit_addabs2_1_rdr0), .clA(control_unit_addabs2_1_cla), .ldR3(control_unit_addabs2_1_ldr3),
    .C0(control_unit_addabs2_1_c0));
  or or_1 (or_1_out, rdR0, control_unit_addabs2_1_rdr0);
  or or_2 (or_2_out, rdR1, control_unit_addabs2_1_rdr1);
  // Probe on in_1
  Operational_Unit operational_unit_1 (
    .rdR3(rdR3), .ldR3(control_unit_addabs2_1_ldr3), .CLK(clock_1_out), .rdR0(or_1_out), .clL(1'b0),
    .ldR0(ldR0), .decA(1'b0), .clA(control_unit_addabs2_1_cla), .incA(1'b0),
    .ldL(control_unit_addabs2_1_ldl), .rdA(control_unit_addabs2_1_rda), .rdALU(control_unit_addabs2_1_rdalu),
    .inBUS(in_2), .rdR1(or_2_out), .DATA_IN(in_1), .sr_A(1'b0), .irA(1'b0), .C0(control_unit_addabs2_1_c0),
    .S(control_unit_addabs2_1_s0), .ldA(control_unit_addabs2_1_lda), .ilA(1'b0), .ldR1(ldR1), .sl_A(1'b0),
    .clR2(1'b0), .incR2(1'b0), .clR3(1'b0), .decR3(1'b0), .F7(operational_unit_1_f7), .DATA_OUT(out_10));  // open: rdR2, ldR2, Z, C, F0, ALL1
  // Probe on out_10

  // Notes on the sheet:
  //   ADDABS2:
  //   R3 <= |R0| + |R1|
endmodule

module Control_Unit_MUL2 (
  input  RESET,
  input  MUL2,
  input  Z,
  input  CLK,
  output rdR2,
  output clA,
  output ldL,
  output S0,
  output ldA,
  output decR3,
  output rdA,
  output ldR1
);

  wire and_1_out, and_2_out, and_3_out, and_4_out, and_5_out, and_6_out, d_ff_1_q, d_ff_3_q, d_ff_5_q,
       not_1_out, not_2_out, or_1_out, or_4_out;

  or or_1 (or_1_out, and_1_out, and_6_out, and_4_out);
  D_FF d_ff_1 (.D(or_1_out), .CLK(CLK), .Sd(RESET), .Q(d_ff_1_q));  // open: Rd, NQ
  not not_1 (not_1_out, MUL2);
  and and_1 (and_1_out, not_1_out, d_ff_1_q);
  and and_2 (and_2_out, MUL2, d_ff_1_q);
  D_FF d_ff_2 (.D(and_2_out), .CLK(CLK), .Rd(RESET), .Q(clA));  // open: Sd, NQ
  or or_2 (rdA, d_ff_3_q, decR3, d_ff_5_q);
  D_FF d_ff_3 (.D(clA), .CLK(CLK), .Rd(RESET), .Q(d_ff_3_q));  // open: Sd, NQ
  or or_3 (ldR1, d_ff_3_q, d_ff_5_q);
  not not_2 (not_2_out, Z);
  and and_3 (and_3_out, not_2_out, d_ff_3_q);
  and and_4 (and_4_out, Z, d_ff_3_q);
  or or_4 (or_4_out, and_3_out, and_5_out);
  D_FF d_ff_4 (.D(or_4_out), .CLK(CLK), .Rd(RESET), .Q(decR3));  // open: Sd, NQ
  D_FF d_ff_5 (.D(decR3), .CLK(CLK), .Rd(RESET), .Q(d_ff_5_q));  // open: Sd, NQ
  and and_5 (and_5_out, not_2_out, d_ff_5_q);
  and and_6 (and_6_out, Z, d_ff_5_q);

  assign ldA = decR3;
  assign ldL = clA;
  assign rdR2 = clA;
  assign S0 = decR3;

  // Notes on the sheet:
  //   K0
  //   K1
  //   K2
  //   K3
  //   K4
endmodule

module MUL2 (
  input  [7:0] in_1,
  input  in_2,
  input  ldR2,
  input  ldR3,
  input  rdR2,
  input  rdR1,
  input  rdR3,
  input  MUL_2,
  input  RESET,
  output [7:0] out_10
);

  wire clock_1_out, control_unit_mul2_1_cla, control_unit_mul2_1_decr3, control_unit_mul2_1_lda,
       control_unit_mul2_1_ldl, control_unit_mul2_1_ldr1, control_unit_mul2_1_rda, control_unit_mul2_1_rdr2,
       operational_unit_1_z, or_1_out;
  wire [0:0] control_unit_mul2_1_s0;

  Clock clock_1 (.out(clock_1_out));
  Control_Unit_MUL2 control_unit_mul2_1 (
    .RESET(RESET), .CLK(clock_1_out), .MUL2(MUL_2), .Z(operational_unit_1_z),
    .rdR2(control_unit_mul2_1_rdr2), .clA(control_unit_mul2_1_cla), .rdA(control_unit_mul2_1_rda),
    .ldL(control_unit_mul2_1_ldl), .ldR1(control_unit_mul2_1_ldr1), .S0(control_unit_mul2_1_s0[0]),
    .ldA(control_unit_mul2_1_lda), .decR3(control_unit_mul2_1_decr3));
  or or_1 (or_1_out, rdR2, control_unit_mul2_1_rdr2);
  // Probe on in_1
  // Probe on out_10
  Operational_Unit operational_unit_1 (
    .rdR3(rdR3), .ldR3(ldR3), .CLK(clock_1_out), .clA(control_unit_mul2_1_cla),
    .ldL(control_unit_mul2_1_ldl), .rdA(control_unit_mul2_1_rda), .inBUS(in_2), .rdR1(rdR1), .DATA_IN(in_1),
    .S({2'b00, control_unit_mul2_1_s0[0]}), .ldA(control_unit_mul2_1_lda), .ldR1(control_unit_mul2_1_ldr1),
    .rdR2(or_1_out), .ldR2(ldR2), .decR3(control_unit_mul2_1_decr3), .Z(operational_unit_1_z),
    .DATA_OUT(out_10));  // open: rdR0, clL, ldR0, decA, incA, rdALU, sr_A, irA, C0, ilA, sl_A, clR2, incR2, clR3, C, F7, F0, ALL1

  // Notes on the sheet:
  //   MUL2:
  //   R1 <= R2 * R3 
  //   (smaller number in R3)
endmodule

module Memory_Cell (
  input  D,
  input  CS,
  input  WR,
  input  RD,
  output Q
);

  wire and_1_out, and_2_out, d_latch_1_q;

  and and_1 (and_1_out, CS, WR);
  and and_2 (and_2_out, CS, RD);
  D_Latch d_latch_1 (.D(D), .E(and_1_out), .Q(d_latch_1_q));  // open: NQ
  assign Q = and_2_out ? d_latch_1_q : 1'bz;  // Controlled_Buffer controlled_buffer_1
endmodule

module Memory_Word_8bit (
  input  WR,
  input  CS,
  input  [7:0] DI,
  input  RD,
  output [7:0] DO
);

  Memory_Cell memory_cell_1 (.D(DI[7]), .CS(CS), .WR(WR), .RD(RD), .Q(DO[7]));
  Memory_Cell memory_cell_2 (.D(DI[6]), .CS(CS), .WR(WR), .RD(RD), .Q(DO[6]));
  Memory_Cell memory_cell_3 (.D(DI[5]), .CS(CS), .WR(WR), .RD(RD), .Q(DO[5]));
  Memory_Cell memory_cell_4 (.D(DI[4]), .CS(CS), .WR(WR), .RD(RD), .Q(DO[4]));
  Memory_Cell memory_cell_5 (.D(DI[3]), .CS(CS), .WR(WR), .RD(RD), .Q(DO[3]));
  Memory_Cell memory_cell_6 (.D(DI[2]), .CS(CS), .WR(WR), .RD(RD), .Q(DO[2]));
  Memory_Cell memory_cell_7 (.D(DI[1]), .CS(CS), .WR(WR), .RD(RD), .Q(DO[1]));
  Memory_Cell memory_cell_8 (.D(DI[0]), .CS(CS), .WR(WR), .RD(RD), .Q(DO[0]));
endmodule

module RAM_2x8b (
  input  [7:0] DI,
  input  A,
  input  RD,
  input  WR,
  input  CS,
  output [7:0] DO
);

  wire [1:0] dc_1to2_1_d;

  DC_1to2 dc_1to2_1 (.E(CS), .S(A), .D(dc_1to2_1_d));
  Memory_Word_8bit memory_word_8bit_1 (.DI(DI), .CS(dc_1to2_1_d[1]), .WR(WR), .RD(RD), .DO(DO));
  Memory_Word_8bit memory_word_8bit_2 (.DI(DI), .CS(dc_1to2_1_d[0]), .WR(WR), .RD(RD), .DO(DO));
endmodule

module RAM_4x8b (
  input  [7:0] DI,
  input  [1:0] A,
  input  WR,
  input  RD,
  input  CS,
  output [7:0] DO
);

  wire [1:0] dc_1to2_1_d;

  DC_1to2 dc_1to2_1 (.E(CS), .S(A[1]), .D(dc_1to2_1_d));
  RAM_2x8b ram_2x8b_1 (.A(A[0]), .CS(dc_1to2_1_d[1]), .DI(DI), .RD(RD), .WR(WR), .DO(DO));
  RAM_2x8b ram_2x8b_2 (.A(A[0]), .CS(dc_1to2_1_d[0]), .DI(DI), .RD(RD), .WR(WR), .DO(DO));
endmodule

module RAM_16x8b (
  input  [7:0] DI,
  input  WR,
  input  CS,
  input  [3:0] A,
  input  RD,
  output [7:0] DO
);

  wire [3:0] dc_2to4_1_d;

  DC_2to4 dc_2to4_1 (.S(A[3:2]), .E(CS), .D(dc_2to4_1_d));
  RAM_4x8b ram_4x8b_1 (.A(A[1:0]), .CS(dc_2to4_1_d[3]), .DI(DI), .WR(WR), .RD(RD), .DO(DO));
  RAM_4x8b ram_4x8b_2 (.A(A[1:0]), .CS(dc_2to4_1_d[2]), .DI(DI), .WR(WR), .RD(RD), .DO(DO));
  RAM_4x8b ram_4x8b_3 (.A(A[1:0]), .CS(dc_2to4_1_d[1]), .DI(DI), .WR(WR), .RD(RD), .DO(DO));
  RAM_4x8b ram_4x8b_4 (.A(A[1:0]), .CS(dc_2to4_1_d[0]), .DI(DI), .WR(WR), .RD(RD), .DO(DO));
endmodule

module RAM_64x8b (
  input  [7:0] DI,
  input  WR,
  input  CS,
  input  [5:0] A,
  input  RD,
  output [7:0] DO
);

  wire [3:0] dc_2to4_1_d;

  DC_2to4 dc_2to4_1 (.S(A[5:4]), .E(CS), .D(dc_2to4_1_d));
  RAM_16x8b ram_16x8b_1 (.A(A[3:0]), .DI(DI), .WR(WR), .RD(RD), .CS(dc_2to4_1_d[3]), .DO(DO));
  RAM_16x8b ram_16x8b_2 (.A(A[3:0]), .DI(DI), .WR(WR), .RD(RD), .CS(dc_2to4_1_d[2]), .DO(DO));
  RAM_16x8b ram_16x8b_3 (.A(A[3:0]), .DI(DI), .WR(WR), .RD(RD), .CS(dc_2to4_1_d[1]), .DO(DO));
  RAM_16x8b ram_16x8b_4 (.A(A[3:0]), .DI(DI), .WR(WR), .RD(RD), .CS(dc_2to4_1_d[0]), .DO(DO));
endmodule

module RAM_256x8b (
  input  [7:0] DI,
  input  WR,
  input  CS,
  input  [7:0] A,
  input  RD,
  output [7:0] DO
);

  wire [3:0] dc_2to4_1_d;

  DC_2to4 dc_2to4_1 (.S(A[7:6]), .E(CS), .D(dc_2to4_1_d));
  RAM_64x8b ram_64x8b_1 (.A(A[5:0]), .DI(DI), .WR(WR), .RD(RD), .CS(dc_2to4_1_d[3]), .DO(DO));
  RAM_64x8b ram_64x8b_2 (.A(A[5:0]), .DI(DI), .WR(WR), .RD(RD), .CS(dc_2to4_1_d[2]), .DO(DO));
  RAM_64x8b ram_64x8b_3 (.A(A[5:0]), .DI(DI), .WR(WR), .RD(RD), .CS(dc_2to4_1_d[1]), .DO(DO));
  RAM_64x8b ram_64x8b_4 (.A(A[5:0]), .DI(DI), .WR(WR), .RD(RD), .CS(dc_2to4_1_d[0]), .DO(DO));
endmodule

module Program_Counter (
  input  [7:0] START_FROM,
  input  PC_Reset,
  input  PC_Write,
  input  CLK,
  input  [7:0] ADR2,
  input  [7:0] ADR1,
  input  [1:0] PC_Src,
  output [7:0] PC_Out
);

  wire or_1_out;
  wire [7:0] inc_8bit_1_f, mp_2to1_8bit_1_d, mp_4to1_8bit_1_d;

  or or_1 (or_1_out, PC_Reset, PC_Write);
  MP_2to1_8bit mp_2to1_8bit_1 (.I1(START_FROM), .I0(mp_4to1_8bit_1_d), .E(1'b1), .S(PC_Reset), .D(mp_2to1_8bit_1_d));
  REG_8bit reg_8bit_1 (
    .INC(1'b0), .DEC(1'b0), .IL(1'b0), .IR(1'b0), .LD(or_1_out), .SR(1'b0), .SL(1'b0), .I(mp_2to1_8bit_1_d),
    .CL(1'b0), .CLK(CLK), .A(PC_Out));
  INC_8bit inc_8bit_1 (.A(PC_Out), .Cin(1'b1), .F(inc_8bit_1_f));  // open: Cout
  MP_4to1_8bit mp_4to1_8bit_1 (
    .I3({8{1'b0}}), .I2(ADR2), .I1(ADR1), .I0(inc_8bit_1_f), .E(1'b1), .S(PC_Src), .D(mp_4to1_8bit_1_d));
endmodule

module Instruction_Register (
  input  [7:0] IN_RAM,
  input  IR_Reset,
  input  IR_Write,
  input  CLK,
  output [3:0] OPCODE,
  output [3:0] OPERAND
);

  REG_8bit reg_8bit_1 (
    .INC(1'b0), .DEC(1'b0), .IL(1'b0), .IR(1'b0), .LD(IR_Write), .SR(1'b0), .SL(1'b0), .I(IN_RAM),
    .CL(IR_Reset), .CLK(CLK), .A({OPCODE, OPERAND}));
endmodule

module Register_File (
  input  RESET,
  input  [7:0] DATA_IN,
  input  [7:0] ALU_IN,
  input  REG_A_Write,
  input  REG_A_Src,
  input  REG_B_Write,
  input  CLK,
  output [7:0] A_OUT,
  output [7:0] B_OUT
);

  wire [7:0] mp_2to1_8bit_1_d;

  MP_2to1_8bit mp_2to1_8bit_1 (.I1(DATA_IN), .I0(ALU_IN), .E(1'b1), .S(REG_A_Src), .D(mp_2to1_8bit_1_d));
  REG_8bit reg_8bit_1 (
    .LD(REG_A_Write), .I(mp_2to1_8bit_1_d), .CL(RESET), .CLK(CLK), .A(A_OUT));  // open: INC, DEC, IL, IR, SR, SL
  REG_8bit reg_8bit_2 (
    .LD(REG_B_Write), .I(DATA_IN), .CL(RESET), .CLK(CLK), .A(B_OUT));  // open: INC, DEC, IL, IR, SR, SL

  // Notes on the sheet:
  //   A
  //   B
endmodule

module Counter2 (
  input  CLK,
  input  RESET,
  output [1:0] Phase
);

  wire d_ff_1_nq, xor_1_out;

  xor xor_1 (xor_1_out, Phase[0], Phase[1]);
  D_FF d_ff_1 (.D(d_ff_1_nq), .CLK(CLK), .Rd(RESET), .Sd(1'b0), .Q(Phase[0]), .NQ(d_ff_1_nq));
  D_FF d_ff_2 (.D(xor_1_out), .CLK(CLK), .Rd(RESET), .Q(Phase[1]));  // open: Sd, NQ
endmodule

module State_Counter_SC (
  input  RESET,
  input  CLK,
  input  E,
  output F0,
  output F1,
  output F2,
  output F3
);

  wire and_1_out;
  wire [1:0] counter2_1_phase;

  Counter2 counter2_1 (.CLK(and_1_out), .RESET(RESET), .Phase(counter2_1_phase));
  and and_1 (and_1_out, E, CLK);
  DC_2to4 dc_2to4_1 (.S(counter2_1_phase), .E(1'b1), .D({F3, F2, F1, F0}));
endmodule

module Control_Unit (
  input  [3:0] OPCODE,
  input  ZERO,
  input  RESET,
  input  CLK,
  output REG_A_Write,
  output REG_B_Write,
  output RAM_Src,
  output PC_Src1,
  output PC_Src,
  output C0,
  output HLT,
  output RAM_Src1,
  output REG_A_Src,
  output WE,
  output PC_Write,
  output IR_Write,
  output [2:0] ALU_OP
);

  wire and_5_out, and_7_out, and_8_out, and_9_out, not_1_out, or_1_out, or_2_out, or_3_out, or_4_out,
       or_6_out, or_7_out, or_8_out, or_9_out, or_10_out, or_11_out, or_12_out, state_counter_sc_1_f1;
  wire [15:0] dc_4to16_1_d;

  DC_4to16 dc_4to16_1 (.S(OPCODE), .E(1'b1), .D(dc_4to16_1_d));
  not not_1 (not_1_out, HLT);
  State_Counter_SC state_counter_sc_1 (
    .E(not_1_out), .RESET(RESET), .CLK(CLK), .F1(state_counter_sc_1_f1), .F0(IR_Write));  // open: F3, F2
  or or_1 (or_1_out, dc_4to16_1_d[1], dc_4to16_1_d[4], dc_4to16_1_d[5], dc_4to16_1_d[6], dc_4to16_1_d[7], dc_4to16_1_d[8], dc_4to16_1_d[9], dc_4to16_1_d[14]);
  and and_1 (REG_A_Write, state_counter_sc_1_f1, or_1_out);
  or or_2 (or_2_out, dc_4to16_1_d[1], dc_4to16_1_d[14]);
  and and_2 (REG_A_Src, state_counter_sc_1_f1, or_2_out);
  or or_3 (or_3_out, dc_4to16_1_d[0], dc_4to16_1_d[3]);
  and and_3 (REG_B_Write, state_counter_sc_1_f1, dc_4to16_1_d[2]);
  and and_4 (WE, state_counter_sc_1_f1, or_3_out);
  and and_5 (and_5_out, state_counter_sc_1_f1, dc_4to16_1_d[12]);
  or or_4 (or_4_out, dc_4to16_1_d[1], dc_4to16_1_d[2], dc_4to16_1_d[3]);
  and and_6 (RAM_Src, state_counter_sc_1_f1, or_4_out);
  or or_5 (PC_Write, IR_Write, and_5_out, and_7_out, and_8_out, and_9_out);
  and and_7 (and_7_out, state_counter_sc_1_f1, ZERO, dc_4to16_1_d[13]);
  and and_8 (and_8_out, state_counter_sc_1_f1, dc_4to16_1_d[10]);
  and and_9 (and_9_out, state_counter_sc_1_f1, ZERO, dc_4to16_1_d[11]);
  and and_10 (PC_Src1, state_counter_sc_1_f1, or_7_out);
  or or_6 (or_6_out, dc_4to16_1_d[12], dc_4to16_1_d[13]);
  or or_7 (or_7_out, dc_4to16_1_d[10], dc_4to16_1_d[11]);
  and and_11 (PC_Src, state_counter_sc_1_f1, or_6_out);
  and and_12 (C0, state_counter_sc_1_f1, or_9_out);
  or or_8 (or_8_out, dc_4to16_1_d[8], dc_4to16_1_d[9]);
  or or_9 (or_9_out, dc_4to16_1_d[4], dc_4to16_1_d[6]);
  or or_10 (or_10_out, dc_4to16_1_d[6], dc_4to16_1_d[7]);
  and and_13 (ALU_OP[2], state_counter_sc_1_f1, or_8_out);
  and and_14 (ALU_OP[1], state_counter_sc_1_f1, or_10_out);
  and and_15 (ALU_OP[0], state_counter_sc_1_f1, or_11_out);
  or or_11 (or_11_out, dc_4to16_1_d[5], dc_4to16_1_d[7], dc_4to16_1_d[9]);
  and and_16 (HLT, state_counter_sc_1_f1, dc_4to16_1_d[15]);
  or or_12 (or_12_out, dc_4to16_1_d[0], dc_4to16_1_d[14]);
  and and_17 (RAM_Src1, state_counter_sc_1_f1, or_12_out);
endmodule
